# Fritzing sketch keyShift (saved by Fritzing 0.9.2b)
breadboards: 1

parts:
  Part1 = Arduino Uno (Rev3)
  7_Segment3 = 7 Segment Display
  U1 = 74HC595 SMD [package="SO16 [SMD]"]

nets:
  N1: Part1.A0, U1.SH_CP
  N2: Part1.A1, U1.ST_CP
  N3: Part1.A2, U1.DS
  5V: Part1.5V, U1.MR, U1.VCC
  N4: 7_Segment3.Segment_G, U1.Q1
  N5: 7_Segment3.Segment_F, U1.Q2
  N6: 7_Segment3.common_anode, U1.GND, U1.OE
  N7: 7_Segment3.Segment_E, U1.Q3
  N8: 7_Segment3.Segment_D, U1.Q4
  N9: 7_Segment3.Segment_DP, U1.Q0
  N10: 7_Segment3.Segment_C, U1.Q5
  N11: 7_Segment3.Segment_B, U1.Q6
  N12: 7_Segment3.Segment_A, U1.Q7
